# Fritzing sketch schematic (saved by Fritzing 0.7.10b)
breadboards: 1

parts:
  XTAL1 = Crystal [frequency="16 Mhz" part_number=16MHz package=THT]
  XTAL2 = Crystal [frequency="2 MHz" part_number=3.579545MHz package=THT]
  C2 = Ceramic Disk Capacitor [part_number=22pF package=THT]
  C1 = Ceramic Disk Capacitor [part_number=22pF package=THT]
  R1 = 100k Ω Resistor [part_number=100K package=THT]
  R2 = 100k Ω Resistor [part_number=100K package=THT]
  C3 = Ceramic Capacitor [part_number=0.1uF package=THT]
  J1 = female pin header, 2 pins [form="♀ (female)" part_number="Audio In"]  # not connected
  R4 = 330k Ω Resistor [part_number=330K package=THT]
  C4 = Ceramic Capacitor [part_number=0.1uF package=THT]
  R5 = 100k Ω Resistor [part_number=100K package=THT]
  C6 = Ceramic Disk Capacitor [part_number=22pF package=THT]
  C5 = Ceramic Disk Capacitor [part_number=22pF package=THT]
  LED2 = LED - 3mm [color="Red (633nm)" part_number=Active package="3 mm [THT]"]
  LED3 = LED - 3mm [color="Red (633nm)" part_number=Inactive package="3 mm [THT]"]
  J2 = Generic male header - 3 pins [part_number="Outputs 2-4" package=THT]
  J3 = Generic male header - 4 pins [part_number="Outputs 5-8" package=THT]
  U1 = atmega328 [package=dip]
  IC1 = IC, DIP package, 18 pins [chip_label=MT8870]
  IC1_2 = IC, DIP package, 18 pins [chip_label=MT8870]
  LED5 = green LED - 5mm [part_number=Decoding package="5 mm [THT]"]
  R7 = 1k Ω Resistor [part_number=1K package=THT]
  J5 = Generic male header - 3 pins [part_number="Outputs 9-11" package=THT]

nets:
  N1: XTAL1.pin_0, C5.pin_1, U1.XLAT1
  N2: XTAL1.pin_1, C6.pin_1, U1.XLAT2
  N3: XTAL2.pin_0, C2.pin_1, IC1.pin8, IC1_2.pin8
  N4: XTAL2.pin_1, C1.pin_1, IC1.pin7, IC1_2.pin7
  GND: C2.pin_0, C1.pin_0, C6.pin_0, C5.pin_0, LED2.cathode, LED3.cathode, U1.GND, IC1.pin5, IC1.pin6, IC1.pin9, IC1_2.pin5, IC1_2.pin6, IC1_2.pin9, R7.Pin_0
  N5: R1.Pin_0, R2.Pin_1, IC1.pin2, IC1_2.pin2
  N6: R1.Pin_1, IC1.pin3, IC1_2.pin3
  N7: R2.Pin_0, C3.pin_0
  N8: R4.Pin_0, IC1.pin16, IC1_2.pin16
  N9: R4.Pin_1, C4.pin_0, IC1.pin17, IC1_2.pin17
  5V: C4.pin_1, R5.Pin_1, U1.VCC, IC1.pin10, IC1.pin18, IC1_2.pin10, IC1_2.pin18
  N10: R5.Pin_0, U1.RESET
  N11: LED2.anode, U1.D13
  N12: LED3.anode, U1.D12
  N13: J2.pin1, U1.D4
  N14: J2.pin2, U1.D3_(PWM)
  N15: J2.pin3, U1.D2
  N16: J3.pin1, U1.D8
  N17: J3.pin2, U1.D7
  N18: J3.pin3, U1.D6_(PWM)
  N19: J3.pin4, U1.D5_(PWM)
  N20: U1.D9_(PWM), J5.pin3
  N21: U1.D10_(PWM), J5.pin2
  N22: U1.D11_(PWM), J5.pin1
  N23: U1.A0, IC1.pin15, IC1_2.pin15, LED5.anode
  N24: U1.A1, IC1.pin14, IC1_2.pin14
  N25: U1.A2, IC1.pin13, IC1_2.pin13
  N26: U1.A3, IC1.pin12, IC1_2.pin12
  N27: U1.A4, IC1.pin11, IC1_2.pin11
  N28: IC1.pin1, IC1.pin4, IC1_2.pin1, IC1_2.pin4
  N29: LED5.cathode, R7.Pin_1
